# Fritzing sketch SoundLights (saved by Fritzing 0.9.3b)
breadboards: 1

parts:
  Part1 = Arduino Nano (Rev3.0)
  neopixel1 = Neopixel Ring 12
  R1 = Resistor [tolerance=±5% resistance=470 package=THT]
  C1 = Electrolytic Capacitor [capacitance=1mF package="100 mil [THT, electrolytic]"]
  S1 = Toggle Switch [package=THT]
  S2 = Pushbutton [package=THT]
  Part2 = Adafruit MAX4466 Electret Microphone Amplifier [part_number=MAX4466]
  R2 = Rotary Potentiometer (Small) [maximum_resistance=10kΩ package=THT]
  R3 = Rotary Potentiometer (Small) [maximum_resistance=10kΩ package=THT]

nets:
  GND: Part1.GND, neopixel1.GND, C1.-, S1.L2, S2.leg1, Part2.GND, R2.leg1, R3.leg1
  N1: Part1.D6, R1.Pin_0
  N2: Part1.D11/MOSI, S1.COM
  N3: Part1.D12/MISO, S2.leg0
  5V: Part1.5V, neopixel1.VCC, C1.+, R2.leg2, R3.leg2
  N4: Part1.A2, R2.wiper
  N5: Part1.A1, R3.wiper
  N6: Part1.A0, Part2.OUT
  3V3: Part1.3V3, Part2.VCC
  N7: neopixel1.IN, R1.Pin_1

custom parts:
  Neopixel Ring 12: Neopixel Ring x12
  Adafruit MAX4466 Electret Microphone Amplifier: Add an ear to your project with this well-designed electret microphone amplifier. This fully assembled and tested board comes with a 20-20KHz electret microphone soldered on. For the amplification, we use the Maxim MAX4466, an op-amp specifically designed for this delicate task! The amplifier has excellent power supply noise rejection, so this amplifier sounds really good and isn't nearly as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
